# Fritzing sketch Calculadora (saved by Fritzing 0.9.10b)

parts:
  Keypad4x1 = Keypad Membran 4x4
  Part1 = Arduino Uno (Rev3) - ICSP
  Part2 = LCD1602-I2C

nets:
  N1: Keypad4x1.Pin1, Part1.D9_PWM
  N2: Keypad4x1.Pin2, Part1.D8
  N3: Keypad4x1.Pin3, Part1.D7
  N4: Keypad4x1.Pin4, Part1.D6_PWM
  N5: Keypad4x1.Pin5, Part1.D5_PWM
  N6: Keypad4x1.Pin6, Part1.D4
  N7: Keypad4x1.Pin7, Part1.D3_PWM
  N8: Keypad4x1.Pin8, Part1.D2
  N9: Part1.A4/SDA, Part2.SDA
  N10: Part1.A5/SCL, Part2.SCL
  5V: Part1.5V, Part2.VCC
  GND: Part1.GND, Part2.GND

custom parts:
  Keypad Membran 4x4: Membrane Keypad 4x4 Matrix
  LCD1602-I2C: A standard character display, usually with 2x16 characters. Comes in many colors with LCM1602 IIC attached.
