# Fritzing sketch Conexiones-Fritzing2 (saved by Fritzing 0.9.6b)

parts:
  L298N1 = L298N DC motor driver
  M1 = DC Motor
  M2 = DC Motor
  Part1 = Arduino Uno (Rev3)
  U1 = LIPO-2000mAh [package=lipo-2000]
  U2 = LIPO-2000mAh [package=lipo-2000]
  FC-1 = Sound Sensor
  M3 = DC Motor
  M4 = DC Motor

nets:
  N1: L298N1.OUT1, M2.pin_2, M4.pin_2
  N2: L298N1.OUT3, M1.pin_2, M3.pin_2
  N3: L298N1.OUT4, M1.pin_1, M3.pin_1
  N4: L298N1.12V, U1.+
  GND: L298N1.GND, Part1.GND, U2.-, FC-1.GND
  5V: L298N1.5V, Part1.5V
  N5: L298N1.ENA, Part1.D11_PWM/MOSI
  N6: L298N1.ENB, Part1.D6_PWM
  N7: L298N1.IN1, Part1.D10_PWM/SS
  N8: L298N1.IN2, Part1.D9_PWM
  N9: L298N1.IN3, Part1.D8
  N10: L298N1.IN4, Part1.D7
  N11: M2.pin_1, M4.pin_1
  N12: Part1.A0, FC-1.OUT
  3V3: Part1.3V3, FC-1.VCC
  N13: U1.-, U2.+

notes:
  2 x 3.7 V LiPo Batteries connected in series
  Motores Derecha
  Motores Izquierda
  L298N Motor Driver Board
  Sensor de Sonido

custom parts:
  L298N DC motor driver: 2x DC motor driver with 78M05 positive voltage regulator (7..35 V) L298N: max 46 V, 2 A Set 5 V Enable jumper to enable 5 V regultor (needed for the L298N) and +5 V output at screw terminal or supply external +5 V at screw terminal Set ENA and/or ENB to +5 V to enable motor permanently or supply ENA and/or ENB with PWM signal IN1 and IN2 set rotation directory for motor A (OUT1/OUT2) IN2 and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
